# Fritzing sketch MagicMirror (saved by Fritzing 0.9.3b)
breadboards: 1

parts:
  Raspberry_Pi_3 = Raspberry Pi 3 [part_number=RPI-3-V1.2]
  DHT22_Temperature-Humidity_Sensor = DHT22 Humidity and Temperature Sensor [part_number=MMM-LocalTemperature]
  Temperature_stability_resistor = Resistor [tolerance=±5% resistance=10k package=THT]
  Power_LED_resistor = Resistor [tolerance=±5% resistance=1k package=THT]
  Debug_Switch = Round Pushbutton [part_number=MMM-ModuleToggle-Button]
  Power_LED = LED - 5mm [color="Green (555nm)" package="5 mm [THT]"]
  HC-SR501 = PIR sensor [part_number=MMM-PIR-Sensor]

nets:
  GND: Raspberry_Pi_3.GND, DHT22_Temperature-Humidity_Sensor.GND, Debug_Switch.leg1, Power_LED.cathode, HC-SR501.GND
  N1: Raspberry_Pi_3.GIPO5, HC-SR501.SIG
  N2: Raspberry_Pi_3.GIPO6, Debug_Switch.leg0
  N3: Raspberry_Pi_3.GIPO13, Power_LED_resistor.Pin_0
  N4: Raspberry_Pi_3.GIPO14, DHT22_Temperature-Humidity_Sensor.DATA, Temperature_stability_resistor.Pin_1
  VDD: Raspberry_Pi_3.5V, DHT22_Temperature-Humidity_Sensor.VDD, Temperature_stability_resistor.Pin_0, HC-SR501.VDD
  N5: Power_LED_resistor.Pin_1, Power_LED.anode
